# Fritzing sketch Schematic (saved by Fritzing 0.9.1b)
breadboards: 1

parts:
  Part1 = Intel Edison Arduinobreakout
  R1 = Photocell (LDR) [package=THT]
  LED1 = LED - 3mm [color="Red (633nm)" package="3 mm [THT]"]
  LED2 = LED - 3mm [color="Green (570nm)" package="3 mm [THT]"]
  R2 = Resistor [tolerance=±5% resistance=680 package=THT]
  R3 = Resistor [tolerance=±5% resistance=680 package=THT]
  R4 = Temperature Sensor (Thermistor) [thermistor_type=NTC package=THT]
  R5 = Resistor [package="0402 [SMD]"]
  R6 = Resistor [package="0402 [SMD]"]

nets:
  N1: Part1.A0, R1.pin_0, R6.Pin_1
  N2: Part1.A1, R4.pin_0, R5.Pin_1
  N3: Part1.D12/MISO, R2.Pin_1
  N4: Part1.D13/SCK, R3.Pin_1
  N5: Part1.5V, R1.pin_1, R4.pin_1
  N6: Part1.GND, LED1.cathode, LED2.cathode, R5.Pin_0, R6.Pin_0
  N7: LED1.anode, R2.Pin_0
  N8: LED2.anode, R3.Pin_0
